# Fritzing sketch Harp Sketch (saved by Fritzing 0.9.3b)
breadboards: 1

parts:
  Arduino = Arduino Uno (Rev3)
  PhotoResistorC = Photocell (LDR) [package=THT]
  PhotoResistorD = Photocell (LDR) [package=THT]
  PhotoResistorE = Photocell (LDR) [package=THT]
  PhotoResistorF = Photocell (LDR) [package=THT]
  PhotoResistorG = Photocell (LDR) [package=THT]
  RC = Resistor [tolerance=±5% resistance=10k package="0402 [SMD]"]
  RD = Resistor [tolerance=±5% resistance=10k package="0402 [SMD]"]
  RE = Resistor [tolerance=±5% resistance=10k package="0402 [SMD]"]
  RF = Resistor [tolerance=±5% resistance=10k package="0402 [SMD]"]
  RG = Resistor [tolerance=±5% resistance=10k package="0402 [SMD]"]
  LD1 = LD
  LD2 = LD
  LD5 = LD
  LD4 = LD
  LD3 = LD
  Часть1 = Bluetooth HC-05 Macho

nets:
  N1: Arduino.A0, PhotoResistorC.pin_1, RC.Pin_0
  N2: Arduino.A1, PhotoResistorD.pin_1, RD.Pin_0
  N3: Arduino.A2, PhotoResistorE.pin_1, RE.Pin_0
  N4: Arduino.A3, PhotoResistorG.pin_1, RF.Pin_0
  N5: Arduino.A4/SDA, PhotoResistorF.pin_1, RG.Pin_0
  GND: Arduino.GND, RC.Pin_1, RD.Pin_1, RE.Pin_1, RF.Pin_1, RG.Pin_1, LD1.cathode, LD2.cathode, LD5.cathode, LD4.cathode, LD3.cathode, Часть1.GND
  N6: Arduino.D2, Часть1.TXD
  N7: Arduino.D3_PWM, Часть1.RXD
  5V: Arduino.5V, PhotoResistorC.pin_0, PhotoResistorD.pin_0, PhotoResistorE.pin_0, PhotoResistorF.pin_0, PhotoResistorG.pin_0, LD1.anode, LD2.anode, LD5.anode, LD4.anode, LD3.anode, Часть1.VCC

custom parts:
  LD: A Generic Red Dot Laser Diode Module (~5mW)
